# Fritzing sketch rainSensor (saved by Fritzing 0.9.4)
circuit board: 6.87817cm x 5.44151cm
breadboards: 1

parts:
  R_zero_w = Raspberry Pi Zero
  MCP3008 = MCP3008 [package=dil16]
  YL-83_-_Detection_Board1 = YL-83 Rain Sensor - Detection Board
  YL-83_-_Control_Board1 = YL-83 Rain Sensor - Control Board
  HLK-PM1 = HLK-PM01

nets:
  VDD: R_zero_w.pin_1, R_zero_w.pin_17, MCP3008.VREF, MCP3008.VDD, YL-83_-_Control_Board1.VCC
  N1: R_zero_w.pin_2, R_zero_w.pin_4, HLK-PM1.+Vo
  N2: R_zero_w.pin_6, R_zero_w.pin_9, R_zero_w.pin_39, MCP3008.DGND, MCP3008.AGND, YL-83_-_Control_Board1.GND, HLK-PM1.-Vo
  N3: R_zero_w.pin_19, MCP3008.Din
  N4: R_zero_w.pin_21, MCP3008.Dout
  N5: R_zero_w.pin_23, MCP3008.CLK
  N6: R_zero_w.pin_24, MCP3008.CS/SHDN
  N7: MCP3008.CH0, YL-83_-_Control_Board1.AO
  N8: YL-83_-_Detection_Board1.POS, YL-83_-_Control_Board1.POS
  N9: YL-83_-_Detection_Board1.NEG, YL-83_-_Control_Board1.NEG

custom parts:
  YL-83 Rain Sensor - Detection Board: The YL-83 is a rain sensor that has more resistance when dry and less resistance when wet. The module runs at 5V.
  YL-83 Rain Sensor - Control Board: The YL-83 is a rain sensor that has more resistance when dry and less resistance when wet. The module runs at 5V.
